# Fritzing sketch diagrama (saved by Fritzing 0.9.3b)
breadboards: 1

parts:
  Raspberry_Pi_1 = Raspberry Pi 3 [part_number=RPI-3-V1.2]
  LED1 = LED - 3mm [color="Green (570nm)" package="3 mm [THT]"]
  LED2 = LED - 3mm [color="Yellow (592nm)" package="3 mm [THT]"]
  LED3 = LED - 3mm [color="Red (660nm)" package="3 mm [THT]"]

nets:
  N1: Raspberry_Pi_1.3v3, Raspberry_Pi_1.GPIO2, LED1.anode
  N2: Raspberry_Pi_1.GPIO3, LED2.anode
  N3: Raspberry_Pi_1.GIPO4, LED3.anode
  N4: Raspberry_Pi_1.GND, LED1.cathode, LED2.cathode, LED3.cathode
